# Fritzing sketch tracker_wiring (saved by Fritzing 0.9.10b)
breadboards: 1

parts:
  U1 = ESP32-38PinWide [part_number=ESP32-38PinWide]
  R1 = PHOTOCELL [package=photocell-kit]  # not connected
  R2 = PHOTOCELL [package=photocell-kit]  # not connected
  R3 = PHOTOCELL [package=photocell-kit]
  R4 = PHOTOCELL [package=photocell-kit]  # not connected
  R6 = Resistor [tolerance=±5% resistance=2.2k package="0805 [SMD]"]
  2_2K = Resistor [tolerance=±5% resistance=2.2k package="0603 [SMD]"]
  Bottom_SERVO = Dagu DGServo 9g (Top view) [part_number=RS001B]
  TOP_SERVO = Dagu DGServo 9g (Top view) [part_number=RS001B]
  R7 = Resistor [tolerance=±5% resistance=100 package="2512 [SMD]"]  # not connected
  R8 = Resistor [tolerance=±5% resistance=2.2k package="0805 [SMD]"]
  2_2K1 = Resistor [tolerance=±5% resistance=2.2k package="0603 [SMD]"]
  R9 = Resistor [tolerance=±5% resistance=100 package="2512 [SMD]"]  # not connected

nets:
  N1: U1.GPIO36, R3.P$2
  N2: U1.GPIO39, 2_2K1.Pin_0
  N3: U1.GPIO34, 2_2K.Pin_0
  N4: U1.GPIO35, R8.Pin_0
  N5: U1.GPIO4, Bottom_SERVO.pulse
  N6: U1.GPIO16, TOP_SERVO.pulse
  N7: U1.GPIO19, R6.Pin_1, 2_2K.Pin_1, R8.Pin_1, 2_2K1.Pin_1

custom parts:
  ESP32-38PinWide: Generic 38-Pin ESP32 with wide format (only access to one side of pins on a breadboard) based on Stephen Lilley's HiLetgo ESP-WROOM-32 ESP32 ESP-32S Development Board.
